# Fritzing sketch fishtank_monitor (saved by Fritzing 1.0.6)
breadboards: 1

parts:
  U1 = ESP32S-HiLetgo [part_number=ESP32S-HiLetgo]
  DS1 = DS18B20 1-Wire Temperature Sensor Probe
  A1 = tds-sensor-meter-v1.0_1
  Q2_-_2N7000 = 2N7000 FET N-Channel [part_number=2N7000 package=TO92]
  R1 = Resistor [tolerance=±5% power=0.25W resistance=47k package=THT]
  R2 = Resistor [tolerance=±5% power=0.25W resistance=10k package=THT]
  Q1_-_S8550 = PNP-Transistor [part_number=S8550 package="TO92 [THT]"]
  R3 = Resistor [tolerance=±5% power=0.25W resistance=100k package=THT]
  S1 = PH meter [package=THT]
  R4 = Resistor [tolerance=±5% power=0.25W resistance=100k package=THT]
  R5 = Resistor [tolerance=±5% power=0.25W resistance=47k package=THT]
  R6 = Resistor [tolerance=±5% power=0.25W resistance=10k package=THT]
  Q3_-_S8550 = PNP-Transistor [part_number=S8550 package="TO92 [THT]"]
  Q4_-_2N7000 = 2N7000 FET N-Channel [part_number=2N7000 package=TO92]
  YwRobot_Power_Supply2 = YwRobot Breadboard Power Supply [part_number=545043]

nets:
  N1: U1.GPIO34, A1.pin1
  N2: U1.GPIO35, S1.pin1
  N3: U1.GPIO25, Q2_-_2N7000.gate, R3.Pin_0
  N4: U1.GPIO26, R4.Pin_0, Q4_-_2N7000.gate
  N5: U1.GND, YwRobot_Power_Supply2.GND#11, YwRobot_Power_Supply2.GND#12
  N6: U1.VIN, YwRobot_Power_Supply2.VCC#5, YwRobot_Power_Supply2.VCC#6
  N7: U1.GPIO4, DS1.DQ
  N8: DS1.GND, A1.pin3, Q2_-_2N7000.source, R3.Pin_1, S1.pin3, R4.Pin_1, Q4_-_2N7000.source, YwRobot_Power_Supply2.GND#13, YwRobot_Power_Supply2.GND#14
  N9: DS1.VDD, R1.Pin_0, Q1_-_S8550.E, R5.Pin_0, YwRobot_Power_Supply2.VCC#9, YwRobot_Power_Supply2.VCC#10
  N10: A1.pin2, Q1_-_S8550.C
  N11: R1.Pin_1, R2.Pin_1, Q1_-_S8550.B
  N12: S1.pin2, Q3_-_S8550.C
  N13: R5.Pin_1, R6.Pin_1, Q3_-_S8550.B

custom parts:
  ESP32S-HiLetgo: HiLetgo ESP-WROOM-32 ESP32 ESP-32S Development Board 2.4GHz Dual-Mode WiFi + Bluetooth Dual Cores Microcontroller The ESP32 integrated with Antenna switches, RF Balun, power amplifiers, low-noise amplifiers, filters, and management modules, and the entire solution occupies the least area of PCB. 2.4 GHz Wi-Fi plus Bluetooth dual-mode chip, with TSMC Ultra-low power consumption 40nm technology,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
  : TDS Meter V1.0 Development Board Water Meter Filter Measuring Water Sensor Module.
  2N7000 FET N-Channel: A 2N7000 MOSFET N-Channel Transistor
  YwRobot Breadboard Power Supply: The YwRobot Breadboard Power Supply (MB-V2) has two power rails; they can be 5V or 3V3. Power to the module can be provided through the female USB socket or through the A10 (female) 2.1mm power jack.
